# Fritzing sketch rgbLED_schematic (saved by Fritzing 0.9.3b)
breadboards: 1

parts:
  Part1 = Arduino Mega 2560 (Rev3)
  R1 = Resistor [tolerance=±5% resistance=220 package=THT]
  R2 = Resistor [tolerance=±5% resistance=220 package=THT]
  R3 = Resistor [tolerance=±5% resistance=220 package=THT]
  LED2 = RGB LED - (4 legs) [package="5 mm [THT]"]

nets (from the breadboard view):
  N1: Part1.GND, LED2.common_anode
  N2: Part1.D3_PWM, Part1.D5_PWM, Part1.D6_PWM
  N3: R1.Pin_0, R2.Pin_0
  N4: R1.Pin_1, LED2.blue_cathode
  N5: R3.Pin_1, LED2.red_cathode
