# Fritzing sketch pushbutton_schematic (saved by Fritzing 0.9.3b)
breadboards: 1

parts:
  Part1 = Arduino Mega 2560 (Rev3)
  R1 = Resistor [tolerance=±5% resistance=220 package=THT]
  S1 = Pushbutton [package=THT]
  LED1 = LED - 5mm [color="Red (633nm)" package="5 mm [THT]"]

nets:
  N1: Part1.D3_PWM, S1.leg0
  N2: R1.Pin_0, S1.leg1
  N3: R1.Pin_1, LED1.anode
  GND: LED1.cathode
