# Fritzing sketch titl_switch_schematic (saved by Fritzing 0.9.3b)
breadboards: 1

parts:
  Part1 = Arduino Mega 2560 (Rev3)
  S1 = Tilt Switch [package=THT]

nets:
  N1: Part1.D3_PWM, S1.Pin_1
  N2: Part1.GND, S1.Pin_2
