# Fritzing sketch passive_buzzer_schematics (saved by Fritzing 0.9.3b)
breadboards: 1

parts:
  Part1 = Arduino Mega 2560 (Rev3)
  SG1 = Buzzer 12mm [package=buzzer-ccv]

nets:
  N1: Part1.GND, SG1.2
  N2: Part1.D28, SG1.1
