# Fritzing sketch servo_motor_schematics (saved by Fritzing 0.9.3b)
breadboards: 1

parts:
  J1 = Basic Servo
  Part1 = Arduino Mega 2560 (Rev3)

nets:
  GND: J1.gnd, Part1.GND
  N1: J1.vcc, Part1.IOREF
  N2: J1.pulse, Part1.D28
