# Fritzing sketch ultrasonic_sensor_schematics (saved by Fritzing 0.9.3b)
breadboards: 1

parts:
  Part1 = Arduino Mega 2560 (Rev3)
  HC-SR04_Sensor_1 = HC-SR04 Ultrasonic Distance Sensor

nets:
  N1: Part1.D12_PWM, HC-SR04_Sensor_1.TRIG
  N2: Part1.D11_PWM, HC-SR04_Sensor_1.GND
  N3: Part1.IOREF, HC-SR04_Sensor_1.VCC
  N4: Part1.GND, HC-SR04_Sensor_1.ECHO
