# Fritzing sketch keypad_schematic (saved by Fritzing 0.9.3b)
breadboards: 1

parts:
  Keypad4x1 = Keypad Membran 4x4
  Part1 = Arduino Mega 2560 (Rev3)
  J1 = female pin header, 8 pins [form="♀ (female)"]

nets (from the schematic view):
  N1: Keypad4x1.Pin1, Keypad4x1.Pin4, Keypad4x1.Pin7, Part1.D6_PWM, J1.pin1, J1.pin4, J1.pin7
  N2: Keypad4x1.Pin3, Keypad4x1.Pin5, Keypad4x1.Pin6, Keypad4x1.Pin8, Part1.D8_PWM, Part1.D7_PWM, J1.pin2, J1.pin3, J1.pin5, J1.pin6, J1.pin8

custom parts:
  Keypad Membran 4x4: Membrane Keypad 4x4 Matrix
