# Fritzing sketch temperature_sensor_schematics (saved by Fritzing 0.9.3b)
breadboards: 1

parts:
  Part1 = Arduino Mega 2560 (Rev3)
  DHT1 = Humidity and Temperature Sensor DHT11

nets:
  N1: Part1.GND, DHT1.GND_2
  5V: Part1.5V, DHT1.Vcc
  N2: Part1.D2_PWM, DHT1.Data-signal

custom parts:
  Humidity and Temperature Sensor DHT11: Digital relative humidity & temperature sensor DHT11
