# Fritzing sketch joystick_module_schematic (saved by Fritzing 0.9.3b)
breadboards: 1

parts:
  Part1 = Arduino Mega 2560 (Rev3)
  Part2 = Thumb Joystick

nets:
  N1: Part1.A0, Part2.VERT
  N2: Part1.A1, Part2.HORZ
  GND: Part1.GND, Part2.GND
  N3: Part1.D2_PWM, Part2.SEL
  5V: Part1.5V, Part2.VCC
