# Fritzing sketch IR_Reciever_schematic (saved by Fritzing 0.9.3b)
breadboards: 1

parts:
  Part1 = Arduino Mega 2560 (Rev3)
  Part2 = IR Receiver Breakout [package=PCB]

nets:
  GND: Part1.GND, Part2.GND
  N1: Part1.D11_PWM, Part2.OUT
  5V: Part1.5V, Part2.VCC
