# Fritzing sketch led_dot_matrix_schematics (saved by Fritzing 0.9.3b)
breadboards: 1

parts:
  Part1 = Arduino Mega 2560 (Rev3)
  8x8_LED_Modul_mit_MAX1 = 8x8 LED Modul mit MAX7219 [package=THT]

nets:
  N1: Part1.GND, 8x8_LED_Modul_mit_MAX1.GND_Eingang
  N2: Part1.D12_PWM, 8x8_LED_Modul_mit_MAX1.DIN_Eingang
  N3: Part1.D11_PWM, 8x8_LED_Modul_mit_MAX1.CS_Eingang
  N4: Part1.D10_PWM, 8x8_LED_Modul_mit_MAX1.CLK_Eingang
  N5: Part1.5V, 8x8_LED_Modul_mit_MAX1.VCC_Eingang
