# Fritzing sketch gyroscope_module_schematics (saved by Fritzing 0.9.3b)
breadboards: 1

parts:
  Part1 = Arduino Mega 2560 (Rev3)
  Part2 = InvenSense MPU6050

nets:
  N1: Part1.D21/SCL, Part1.SCL, Part2.SCL
  N2: Part1.SDA, Part2.SDA
  GND: Part1.GND, Part2.GND
  3V3: Part1.3V3, Part2.VCC
