# Fritzing sketch PIR_sensor_schematics (saved by Fritzing 0.9.3b)
breadboards: 1

parts:
  Part1 = Arduino Mega 2560 (Rev3)
  Part2 = HC-SR501 Body Sensor Module

nets:
  N1: Part1.IOREF, Part2.GND
  N2: Part1.D7_PWM, Part2.VCC

custom parts:
  HC-SR501 Body Sensor Module: Pyroelectric Infrared PIR Motion Sensor Detector Module
