# Fritzing sketch water_sensor_schematic (saved by Fritzing 0.9.3b)
breadboards: 1

parts:
  Part1 = Arduino Mega 2560 (Rev3)
  Water_Level_Sensor1 = Water Level Sensor

nets:
  N1: Part1.A0, Water_Level_Sensor1.SIG
  GND: Part1.GND, Water_Level_Sensor1.GND
  N2: Part1.IOREF, Water_Level_Sensor1.VCC

custom parts:
  Water Level Sensor: A water level sensor. This sensor operates at 3V to 5V. The Sig (signal) pin outputs an analogue signal that is in proportion to the amount of water in contact with the sensor.
