# Fritzing sketch rtc_module_schematics (saved by Fritzing 0.9.3b)
breadboards: 1

parts:
  Part1 = Arduino Mega 2560 (Rev3)
  Part2 = Real Time Clock Module - DS1307 RTC Breakout Board

nets:
  N1: Part1.D21/SCL, Part2.SCL
  N2: Part1.SDA, Part2.SDA
  5V: Part1.5V, Part2.5V
  GND: Part1.GND, Part2.GND
