# Fritzing sketch relay_module_schematics (saved by Fritzing 0.9.3b)
breadboards: 1

parts:
  Part1 = Arduino Mega 2560 (Rev3)
  IC1 = L293D [package=THT]
  L1 = Inductor [package="400 mil [THT]"]  # not connected
  M1 = DC Motor
  S1 = SWITCH-MOMENTARY-2 [package=tactile_switch_smd-2]

nets:
  N1: Part1.D3_PWM, IC1.In_2
  N2: Part1.D4_PWM, IC1.In_1
  N3: Part1.D5_PWM, IC1.Enable_1
  N4: IC1.Out_1_(_Controlled_by_Enable_1_), IC1.Out_2_(_Controlled_by_Enable_1_)
  GND: IC1.0V, M1.pin_2
  5V: IC1.+Vmotor, S1.1
  N5: M1.pin_1, S1.2
