# Fritzing sketch remote_stepper_motor_schematics (saved by Fritzing 0.9.3b)
breadboards: 1

parts:
  5V = Power plug
  MOTOR1 = 28BYJ-48 Stepper Motor
  X1 = X113647 Stepper Driver Board [part_number=X113647 package=board]
  Part1 = Arduino Mega 2560 (Rev3)
  Part2 = IR Receiver Breakout [package=PCB]

nets:
  GND: 5V.GND, X1.GND, Part2.GND
  N1: 5V.VCC, X1.+V
  N2: MOTOR1.BLUE, X1.BLUE
  N3: MOTOR1.PINK, X1.PINK
  N4: MOTOR1.RED, X1.RED
  N5: MOTOR1.ORANGE, X1.ORANGE
  N6: MOTOR1.YELLOW, X1.YELLOW
  N7: X1.IN1, Part1.D11_PWM
  N8: X1.IN2, Part1.D10_PWM
  N9: X1.IN3, Part1.D9_PWM
  N10: X1.IN4, Part1.D8_PWM
  N11: Part1.D12_PWM, Part2.OUT
  5V: Part1.5V, Part2.VCC

custom parts:
  28BYJ-48 Stepper Motor: 28BYJ-48 gear-reduction stepper motor (small)
  X113647 Stepper Driver Board: A common stepper motor driver board based on ULN2003APG darlington array
