# Fritzing sketch motor_rotor_encoder (saved by Fritzing 0.9.3b)
breadboards: 1

parts:
  Part1 = Arduino Mega 2560 (Rev3)
  RE1 = KY-040 Rotary encoder [package=THT]
  MOTOR2 = 28BYJ-48 Stepper Motor
  X2 = X113647 Stepper Driver Board [part_number=X113647 package=board]
  5V1 = Power plug

nets:
  GND: Part1.GND, RE1.GND
  N1: Part1.D11_PWM, X2.IN1
  N2: Part1.D10_PWM, X2.IN2
  N3: Part1.D9_PWM, X2.IN3
  N4: Part1.D8_PWM, X2.IN4
  5V: Part1.5V, RE1.Vcc
  N5: Part1.D2_PWM, RE1.CLK
  N6: Part1.D3_PWM, RE1.DT
  N7: Part1.D4_PWM, RE1.SW
  N8: MOTOR2.BLUE, X2.BLUE
  N9: MOTOR2.PINK, X2.PINK
  N10: MOTOR2.RED, X2.RED
  N11: MOTOR2.ORANGE, X2.ORANGE
  N12: MOTOR2.YELLOW, X2.YELLOW
  GND_2: X2.GND, 5V1.GND
  N13: X2.+V, 5V1.VCC

custom parts:
  KY-040 Rotary encoder: KY-040 Rotary Encoder with switch on breakout borad from AZ Delivery
  28BYJ-48 Stepper Motor: 28BYJ-48 gear-reduction stepper motor (small)
  X113647 Stepper Driver Board: A common stepper motor driver board based on ULN2003APG darlington array
