# Fritzing sketch sound_sensor_schematic (saved by Fritzing 0.9.3b)
breadboards: 1

parts:
  Part1 = Arduino Mega 2560 (Rev3)
  FC-1 = Sound Sensor

nets:
  N1: Part1.A0, FC-1.OUT
  GND: Part1.GND, FC-1.GND
  N2: Part1.IOREF, FC-1.VCC
