# Fritzing sketch gps_module_schematics (saved by Fritzing 0.9.3b)
breadboards: 1

parts:
  Part1 = Arduino Mega 2560 (Rev3)
  GY-NEO6MV3 = SUP500F [package=sup500f]

nets:
  GND: Part1.GND, GY-NEO6MV3.GND
  5V: Part1.5V, GY-NEO6MV3.VCC
  N1: Part1.D3_PWM, GY-NEO6MV3.TX-O
  N2: Part1.D4_PWM, GY-NEO6MV3.RX-I
