# Fritzing sketch schematic (saved by Fritzing 0.9.3b)
breadboards: 1

parts:
  Part1 = Arduino Mega 2560 (Rev3)
  Part2 = NRF24L01

nets:
  N1: Part1.D13_PWM, Part2.SCK
  N2: Part1.D12_PWM, Part2.MISO
  N3: Part1.D11_PWM, Part2.MOSI
  N4: Part1.D10_PWM, Part2.IRQ
  N5: Part1.D9_PWM, Part2.CE
  N6: Part1.D8_PWM, Part2.CSN
  3V3: Part1.3V3, Part2.VCC
  GND: Part1.GND, Part2.GND
