# Fritzing sketch schematics (saved by Fritzing 0.9.3b)
breadboards: 1

parts:
  Mod1 = AD8232 HeartRate Monitor [part_number=SEN-12650]
  Part1 = Arduino Mega 2560 (Rev3)

nets:
  GND: Mod1.GND, Part1.GND
  3.3V: Mod1.3.3v, Part1.3V3
  N1: Mod1.OUTPUT, Part1.A0
  N2: Mod1.LO-, Part1.D11_PWM
  N3: Mod1.LO+, Part1.D10_PWM

custom parts:
  AD8232 HeartRate Monitor: Sparkfun single lead heart rate monitor - Ad8232.
